# Fritzing sketch Pico mit TPL (saved by Fritzing 1.0.3b)
breadboards: 1

parts:
  Mod1 = Raspberry Pi Pico W
  Bauteil1 = Adafruit TPL5111 Reset Enable Timer [part_number="Adafruit #3573"]
  U2 = LIPO-2000mAh [package=lipo-2000]
  DHT1 = DHT22 Humidity and Temperature Sensor
  R1 = Resistor [tolerance=±5% power=0.25W resistance=220 package=THT]
  R2 = Resistor [tolerance=±5% power=0.25W resistance=220 package=THT]
  R3 = Resistor [tolerance=±5% power=0.25W resistance=220 package=THT]

nets:
  GND: Mod1.pin_3, Mod1.pin_8, Mod1.pin_13, Mod1.pin_18, Mod1.pin_23, Mod1.pin_28, Mod1.pin_33, Mod1.pin_38, Mod1.pin_42, Bauteil1.GND, Bauteil1.DONE, U2.-, DHT1.GND, R2.Pin_0, R3.Pin_1
  N1: Mod1.pin_20, DHT1.DATA, DHT1.NULL
  N2: Mod1.pin_31, R2.Pin_1
  N3: Mod1.pin_36, DHT1.VDD
  N4: Mod1.pin_37, Bauteil1.ENOUT
  N5: Mod1.pin_39, Bauteil1.VDD, U2.+, R1.Pin_1
  N6: Bauteil1.DELAY, R3.Pin_0

custom parts:
  Raspberry Pi Pico W: Raspberry Pi Pico W. Based around the RP2040 microcontroller the Pico W is a low cost microcontroller device bringing Raspberry Pi quality, cost, and easy of use to the microcontroller space. The areas marked KEEPOUT in pcb silkscreen should not have traces running through them to avoid shorts on a soldered in module!
  Adafruit TPL5111 Reset Enable Timer: The Adafruit TPL5111 Reset Enable Timer is a stand-alone breakout that will turn any electronics into low-power electronics! It will take care of enabling & disabling your electronics using a built in timer that can vary from once-every 100ms up to once every two hours. Basically, the TPL will set an enable pin high periodically, adjustable by potentiometer or resistor, and turn on your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
